# Fritzing sketch ConnectionDiagram_DSMR5_Pico2W (saved by Fritzing 1.0.6)
circuit board: 8.46667cm x 5.64444cm
breadboards: 1

parts:
  A1 = Raspberry Pi Pico2
  J1 = RJ11 Jack [package=rj11-6]

nets:
  N1: A1.pin_2, J1.5
  N2: A1.pin_3, A1.pin_8, A1.pin_13, A1.pin_18, A1.pin_23, A1.pin_28, A1.pin_33, A1.pin_38, J1.3, J1.6
  N3: J1.1, J1.2

custom parts:
  Raspberry Pi Pico2: Raspberry Pi Pico 2W is our new $7 microcontroller board, built on RP2350: our new high-performance, secure microcontroller with on board WiFi.
